# Fritzing sketch wiring (saved by Fritzing 0.9.3b)
breadboards: 1

parts:
  U1 = NodeMCU V3.0
  C1 = Electrolytic Capacitor [capacitance=470µF package="200 mil [THT, electrolytic]"]
  Part1 = Logic Level Converter
  R1 = Resistor [tolerance=±5% resistance=220 package="0603 [SMD]"]
  U2 = WS2812 RGB LED strip

nets:
  N1: U1.D2, Part1.RX2_LV
  N2: U1.3V3, Part1.LV
  GND: U1.GND, C1.-, Part1.GND, U2.GND
  N3: U1.VU, C1.+, Part1.HV, U2.VCC
  N4: Part1.RX2_HV, R1.Pin_1
  N5: R1.Pin_0, U2.DIN

custom parts:
  NodeMCU V3.0: ESP8266 based NodeMCU
  WS2812 RGB LED strip: WS2812 strip
